# Fritzing sketch AR12_4LED.. (saved by Fritzing 0.9.3b)
breadboards: 1

parts:
  부품1 = Arduino Uno (Rev3)
  LED1 = LED - 5mm [color="Blue (470nm)" package="5 mm [THT]"]
  LED2 = LED - 5mm [color="Infrared (850nm)" package="5 mm [THT]"]
  LED3 = LED - 5mm [color="Yellow (595nm)" package="5 mm [THT]"]
  LED4 = LED - 5mm [color="Red (633nm)" package="5 mm [THT]"]
  R3 = Resistor [tolerance=±5% resistance=220 package=THT]
  R4 = Resistor [tolerance=±5% resistance=220 package=THT]
  R5 = Resistor [tolerance=±5% resistance=220 package=THT]
  R6 = Resistor [tolerance=±5% resistance=220 package=THT]

nets:
  N1: 부품1.D9_PWM, LED3.cathode
  N2: 부품1.D3_PWM, LED4.cathode
  N3: 부품1.D5_PWM, LED2.cathode
  N4: 부품1.D6_PWM, LED1.cathode
  N5: 부품1.GND, R3.Pin_1, R4.Pin_1, R5.Pin_1, R6.Pin_1
  N6: LED1.anode, R4.Pin_0
  N7: LED2.anode, R6.Pin_0
  N8: LED3.anode, R3.Pin_0
  N9: LED4.anode, R5.Pin_0
